# Fritzing sketch DesignICAss (saved by Fritzing 0.9.4)
circuit board: 8.46667cm x 5.64444cm
breadboards: 1

parts:
  U1 = 555 Timer [package="DIP8 [THT]"]
  LED1 = LED - 5mm [color="Red (633nm)" current=0.030 package="5 mm [THT]"]
  LED2 = LED - 5mm [color="Red (633nm)" current=0.030 package="5 mm [THT]"]
  LED3 = LED - 5mm [color="Green (565nm)" current=0.030 package="5 mm [THT]"]
  LED4 = LED - 5mm [color="Green (565nm)" current=0.030 package="5 mm [THT]"]
  S1 = Pushbutton [package="[THT]"]
  U2 = LIPO-1000mAh [package=lipo-1000]
  R1 = Resistor [tolerance=±5% power=0.25 resistance=220 package=THT]
  R2 = Resistor [tolerance=±5% power=0.25 resistance=220 package=THT]
  U3 = 74HC04_HEX_INVERTER [package=dil14]
  R3 = Resistor [tolerance=±5% power=0.25 resistance=220 package=THT]
  R4 = Resistor [tolerance=±5% power=0.25 resistance=220 package=THT]
  R5 = Resistor [tolerance=±5% power=0.25 resistance=91k package=THT]
  C2 = Electrolytic Capacitor [capacitance=0.1mF voltage=35V package="100 mil [THT, electrolytic]"]
  C3 = Ceramic Capacitor [capacitance=10nF voltage=35V package="100 mil [THT, multilayer]"]
  R8 = Resistor [tolerance=±5% power=0.25 resistance=91k package=THT]

nets:
  N1: U1.Ground, LED1.cathode, LED2.cathode, LED3.cathode, LED4.cathode, S1.Pin_3, S1.Pin_4, U2.-, U3.GND, C2.-, C3.0
  N2: U1.Trigger, S1.Pin_1, S1.Pin_2, R8.Pin_0
  N3: U1.Output, R1.Pin_0, R2.Pin_0, U3.1A, U3.2A
  N4: U1.Reset, U1.Vcc_Supply_Voltage, U2.+, U3.VCC, R5.Pin_1, R8.Pin_1
  N5: U1.Control_Voltage, C3.1
  N6: U1.Threshold, U1.Discharge, R5.Pin_0, C2.+
  N7: LED1.anode, R1.Pin_1
  N8: LED2.anode, R4.Pin_1
  N9: LED3.anode, R3.Pin_1
  N10: LED4.anode, R2.Pin_1
  N11: U3.1Y, R4.Pin_0
  N12: U3.2Y, R3.Pin_0

notes:
  traffic
  Crossing
  91 kOhm, 100 uF
